# Fritzing sketch moids_infinity_version1 (saved by Fritzing 0.9.3b)
breadboards: 1

parts:
  U1 = MIC [package=mic_electret_smd]
  V1 = DC Power [voltage=5]
  C1 = Ceramic Capacitor [capacitance=0.1µF package="1206 [SMD, multilayer]"]
  R1 = Resistor [tolerance=±5% resistance=10k package="1206 [SMD]"]
  R2 = Resistor [tolerance=±5% resistance=1k package="1206 [SMD]"]
  R3 = Resistor [tolerance=±5% resistance=10k package="1206 [SMD]"]
  R4 = Resistor [tolerance=±5% resistance=10k package="1206 [SMD]"]
  R5 = Resistor [tolerance=±5% resistance=1M package="1206 [SMD]"]
  C2 = Ceramic Capacitor [capacitance=560pF package="1206 [SMD, multilayer]"]
  C3 = Ceramic Capacitor [capacitance=0.1µF package="1206 [SMD, multilayer]"]
  C4 = Ceramic Capacitor [capacitance=0.1µF package="1206 [SMD, multilayer]"]
  U2 = LM358 [package=dip08]
  R6 = Resistor [tolerance=±5% resistance=100k package="1206 [SMD]"]
  D1 = Diode [package=sma-diode]
  R7 = Resistor [tolerance=±5% resistance=1M package="1206 [SMD]"]
  C5 = Ceramic Capacitor [capacitance=0.1µF package="1206 [SMD, multilayer]"]
  C6 = Electrolytic Capacitor [capacitance=470µF package="1010 [SMD, electrolytic]"]
  C7 = Ceramic Capacitor [capacitance=0.1µF package="1206 [SMD, multilayer]"]
  R8 = Resistor [tolerance=±5% resistance=2.2M package="1206 [SMD]"]
  R9 = Resistor [tolerance=±5% resistance=200k package="1206 [SMD]"]
  R10 = Resistor [tolerance=±5% resistance=1k package="1206 [SMD]"]
  Q1 = NPN-Transistor [part_number=C1815 package="TO92 [THT]"]
  R11 = Resistor [tolerance=±5% resistance=10k package="1206 [SMD]"]
  U3 = 555 Timer [package="DIP8 [THT]"]
  C8 = Ceramic Capacitor [capacitance=0.1µF package="1206 [SMD, multilayer]"]
  R12 = Resistor [tolerance=±5% resistance=330k package="1206 [SMD]"]
  C9 = Electrolytic Capacitor [capacitance=10µF package="1010 [SMD, electrolytic]"]
  R13 = Resistor [tolerance=±5% resistance=10k package="1206 [SMD]"]
  C10 = Electrolytic Capacitor [capacitance=10µF package="1010 [SMD, electrolytic]"]
  Q2 = NPN-Transistor [part_number=C1815 package="TO92 [THT]"]
  R14 = Resistor [tolerance=±5% resistance=1k package="1206 [SMD]"]
  Q3 = PNP-Transistor [package="TO92 [THT]"]
  Q4 = TRANSISTOR_NPN [part_number=2N2222A package=to-92]
  R15 = Resistor [tolerance=±5% resistance=10k package="1206 [SMD]"]
  R16 = Resistor [tolerance=±5% resistance=1M package="1206 [SMD]"]
  C11 = Ceramic Capacitor [capacitance=560pF package="1206 [SMD, multilayer]"]
  Q5 = NPN-Transistor [part_number=C1815 package="TO92 [THT]"]
  R17 = Resistor [tolerance=±5% resistance=1k package="1206 [SMD]"]
  R18 = Resistor [tolerance=±5% resistance=1k package="1206 [SMD]"]

nets:
  N1: U1.1, C1.0, R1.Pin_0
  GND: U1.2, V1.V-, R4.Pin_1, C3.1, U2.G$1_V-, R6.Pin_1, R7.Pin_1, C5.1, C6.-, C7.1, R9.Pin_1, Q1.E, U3.Ground, C8.1, C9.-, C10.-, Q2.E, Q4.E, R16.Pin_1, R18.Pin_1
  5V: V1.V+, R1.Pin_1, R3.Pin_0, U2.G$1_V+, C6.+, C7.0, R11.Pin_0, U3.Vcc_Supply_Voltage, R12.Pin_0, R15.Pin_0
  N2: C1.1, R2.Pin_0
  mute: R2.Pin_1, R5.Pin_0, C2.0, U2.G$1_-IN, Q5.C
  N3: R3.Pin_1, R4.Pin_0, C3.0, U2.G$1_+IN
  N4: R5.Pin_1, C2.1, C4.0, U2.G$1_OUT
  N5: C4.1, R6.Pin_0, D1.A
  N6: U2.G$2_+IN, D1.C, R7.Pin_0, C5.0
  N7: U2.G$2_-IN, R8.Pin_0, R9.Pin_0, C11.0
  N8: U2.G$2_OUT, R8.Pin_1, R10.Pin_0, C11.1
  N9: R10.Pin_1, Q1.B
  N10: Q1.C, R11.Pin_1, U3.Trigger
  N11: U3.Output, R13.Pin_0
  N12: U3.Control_Voltage, C8.0
  N13: U3.Threshold, U3.Discharge, R12.Pin_1, C9.+
  N14: R13.Pin_1, C10.+, Q2.B, R17.Pin_1
  N15: Q2.C, R14.Pin_1
  N16: R14.Pin_0, Q3.B
  N17: Q3.E, R15.Pin_1
  N18: Q3.C, Q4.B, R16.Pin_0
  N19: Q5.E, R18.Pin_0
  N20: Q5.B, R17.Pin_0

notes:
  DELAY => R13,C10
  TIME =>  R12,C9
  JACOB
