# Fritzing sketch moids_infinity_version2 (saved by Fritzing 0.9.3b)
breadboards: 1

parts:
  R1 = Resistor [tolerance=±5% resistance=10k package="1206 [SMD]"]
  R2 = Resistor [tolerance=±5% resistance=1k package="1206 [SMD]"]
  R3 = Resistor [tolerance=±5% resistance=10k package="1206 [SMD]"]
  R4 = Resistor [tolerance=±5% resistance=10k package="1206 [SMD]"]
  R5 = Resistor [tolerance=±5% resistance=1M package="1206 [SMD]"]
  C2 = Ceramic Capacitor [capacitance=560pF package="1206 [SMD, multilayer]"]
  C4 = Ceramic Capacitor [capacitance=0.1µF package="1206 [SMD, multilayer]"]
  R6 = Resistor [tolerance=±5% resistance=100k package="1206 [SMD]"]
  R7 = Resistor [tolerance=±5% resistance=1M package="1206 [SMD]"]
  C5 = Ceramic Capacitor [capacitance=0.1µF package="1206 [SMD, multilayer]"]
  C7 = Ceramic Capacitor [capacitance=0.1µF package="1206 [SMD, multilayer]"]
  R8 = Resistor [tolerance=±5% resistance=2.2M package="1206 [SMD]"]
  R9 = Resistor [tolerance=±5% resistance=200k package="1206 [SMD]"]
  R10 = Resistor [tolerance=±5% resistance=1k package="1206 [SMD]"]
  R11 = Resistor [tolerance=±5% resistance=10k package="1206 [SMD]"]
  C8 = Ceramic Capacitor [capacitance=0.1µF package="1206 [SMD, multilayer]"]
  R12 = Resistor [tolerance=±5% resistance=330k package="1206 [SMD]"]
  R13 = Resistor [tolerance=±5% resistance=10k package="1206 [SMD]"]
  R14 = Resistor [tolerance=±5% resistance=1k package="1206 [SMD]"]
  R15 = Resistor [tolerance=±5% resistance=10k package="1206 [SMD]"]
  R16 = Resistor [tolerance=±5% resistance=1M package="1206 [SMD]"]
  C11 = Ceramic Capacitor [capacitance=560pF package="1206 [SMD, multilayer]"]
  R17 = Resistor [tolerance=±5% resistance=1k package="1206 [SMD]"]
  R18 = Resistor [tolerance=±5% resistance=1k package="1206 [SMD]"]
  U2 = LMV358 [package=so08]
  Q5 = NPN-Transistor [package="SOT-23 [SMD]"]
  Q1 = NPN-Transistor [package="SOT-23 [SMD]"]
  Q2 = NPN-Transistor [package="SOT-23 [SMD]"]
  U3 = 555 Timer [package="SO8 [SMD]"]
  C10 = Electrolytic Capacitor [capacitance=10µF package="0405 [SMD, electrolytic]"]
  C9 = Electrolytic Capacitor [capacitance=10µF package="0405 [SMD, electrolytic]"]
  C6 = Electrolytic Capacitor [capacitance=470µF package="0405 [SMD, electrolytic]"]
  C1 = Ceramic Capacitor [capacitance=0.1µF package="0805 [SMD, multilayer]"]
  C3 = Ceramic Capacitor [capacitance=0.1µF package="0805 [SMD, multilayer]"]
  D1 = Diode [package=sma-diode-kit]
  JP4 = Header 2 [package=jst-2-pth-ns]
  JP5 = Header 2 [package=jst-2-pth-ns]
  JP6 = Header 2 [package=jst-2-pth-ns]
  Q4 = TRANSISTOR_NPN [part_number=1815 package=sot23]
  Q3 = PNP-Transistor [package="SOT-23 [SMD]"]
  C12 = Electrolytic Capacitor [capacitance=220µF package="0405 [SMD, electrolytic]"]

nets:
  N1: R1.Pin_0, C1.0, JP5.1
  5V: R1.Pin_1, R3.Pin_0, C7.0, R11.Pin_0, R12.Pin_0, R15.Pin_0, U2.G$1_+V, U3.Pin_8, C6.+, JP4.1, JP6.1, C12.+
  N2: R2.Pin_0, C1.1
  N3: R2.Pin_1, U2.G$1_-IN1
  N4: R3.Pin_1, R4.Pin_0, U2.G$1_+IN1, C3.0
  GND: R4.Pin_1, R6.Pin_1, R7.Pin_1, C5.1, C7.1, R9.Pin_1, C8.1, R16.Pin_1, R18.Pin_1, U2.G$1_GND, Q1.2, Q2.2, U3.Pin_1, C10.-, C9.-, C3.1, JP5.2, Q4.E, C12.-
  mute: R5.Pin_0, C2.0, Q5.1
  N5: R5.Pin_1, C2.1
  N6: C4.0, U2.G$1_OUT1
  N7: C4.1, R6.Pin_0, D1.A
  N8: R7.Pin_0, C5.0, U2.G$2_-IN2, D1.C
  N9: R8.Pin_0, R9.Pin_0, C11.0, U2.G$2_+IN2
  N10: R8.Pin_1, R10.Pin_0, C11.1, U2.G$2_OUT2
  N11: R10.Pin_1, Q1.0
  N12: R11.Pin_1, Q1.1, U3.Pin_2
  N13: C8.0, U3.Pin_5
  N14: R12.Pin_1, U3.Pin_6, U3.Pin_7, C9.+
  N15: R13.Pin_0, U3.Pin_3
  N16: R13.Pin_1, R17.Pin_1, Q2.0, C10.+
  N17: R14.Pin_0, Q3.0
  N18: R14.Pin_1, Q2.1
  N19: R15.Pin_1, Q3.2
  N20: R16.Pin_0, Q4.B, Q3.1
  N21: R17.Pin_0, Q5.0
  N22: R18.Pin_0, Q5.2
  N23: C6.-, JP6.2
  N24: JP4.2, Q4.C

notes:
  DELAY => R13,C10
  TIME =>  R12,C9
  JACOB
