# Fritzing sketch moids_infinity_with_pcb (saved by Fritzing 0.9.3b)
circuit board: 8cm x 4cm
breadboards: 1

parts:
  U1 = LMV358 [package=so08]
  Q5 = NPN-Transistor [package="SOT-23 [SMD]"]
  Q1 = NPN-Transistor [package="SOT-23 [SMD]"]
  Q2 = NPN-Transistor [package="SOT-23 [SMD]"]
  Q3 = PNP-Transistor [package="SOT-23 [SMD]"]
  U2 = 555 Timer [package="SO8 [SMD]"]
  R1 = Resistor [tolerance=±5% resistance=10k package="0603 [SMD]"]
  C3 = Ceramic Capacitor [capacitance=0.1µF package="0603 [SMD, multilayer]"]
  R2 = Resistor [tolerance=±5% resistance=1k package="0603 [SMD]"]
  C4 = Ceramic Capacitor [capacitance=0.1µF package="0603 [SMD, multilayer]"]
  R4 = Resistor [tolerance=±5% resistance=10k package="0603 [SMD]"]
  C5 = Ceramic Capacitor [capacitance=560pF package="0603 [SMD, multilayer]"]
  R6 = Resistor [tolerance=±5% resistance=1M package="0603 [SMD]"]
  R5 = Resistor [tolerance=±5% resistance=200k package="0603 [SMD]"]
  R7 = Resistor [tolerance=±5% resistance=2.2M package="0603 [SMD]"]
  C7 = Ceramic Capacitor [capacitance=0.1µF package="0603 [SMD, multilayer]"]
  C9 = Ceramic Capacitor [capacitance=0.1µF package="0603 [SMD, multilayer]"]
  R8 = Resistor [tolerance=±5% resistance=100k package="0603 [SMD]"]
  R9 = Resistor [tolerance=±5% resistance=1M package="0603 [SMD]"]
  C10 = Ceramic Capacitor [capacitance=0.1µF package="0603 [SMD, multilayer]"]
  R10 = Resistor [tolerance=±5% resistance=1k package="0603 [SMD]"]
  R11 = Resistor [tolerance=±5% resistance=10k package="0603 [SMD]"]
  D1 = Diode [package=sod-323]
  R12 = Resistor [tolerance=±5% resistance=330k package="0603 [SMD]"]
  C12 = Ceramic Capacitor [capacitance=0.1µF package="0603 [SMD, multilayer]"]
  C1 = Tantalum Capacitor [capacitance=470µF package="D 7343 [SMD, tantalum]"]
  R13 = Resistor [tolerance=±5% resistance=10k package="0603 [SMD]"]
  R17 = Resistor [tolerance=±5% resistance=10k package="0603 [SMD]"]
  R16 = Resistor [tolerance=±5% resistance=1k package="0603 [SMD]"]
  R18 = Resistor [tolerance=±5% resistance=1M package="0603 [SMD]"]
  C2 = Tantalum Capacitor [capacitance=470µF voltage=16V package="D 7343 [SMD, tantalum]"]
  R15 = Resistor [tolerance=±5% resistance=1k package="0603 [SMD]"]
  R14 = Resistor [tolerance=±5% resistance=1k package="0603 [SMD]"]
  C13 = Ceramic Capacitor [capacitance=10µF package="0603 [SMD, multilayer]"]
  R3 = Resistor [tolerance=±5% resistance=10k package="0603 [SMD]"]
  C6 = Ceramic Capacitor [capacitance=560pF package="0603 [SMD, multilayer]"]
  C11 = Ceramic Capacitor [capacitance=10µF package="0603 [SMD, multilayer]"]
  JP2 = Header 2 [package=jst-2-smd]
  JP1 = Header 2 [package=jst-2-smd]
  Q4 = NPN-Transistor [package="SOT-23 [SMD]"]
  JP3 = Header 2 [package=jst-2-smd]
  J1 = Resistor [tolerance=±5% resistance=0 package="1206 [SMD]"]
  J2 = Resistor [tolerance=±5% resistance=0 package="1206 [SMD]"]
  J3 = Resistor [tolerance=±5% resistance=0 package="1206 [SMD]"]
  J4 = Resistor [tolerance=±5% resistance=0 package="1206 [SMD]"]
  J5 = Resistor [tolerance=±5% resistance=0 package="1206 [SMD]"]
  J6 = Resistor [tolerance=±5% resistance=0 package="1206 [SMD]"]
  J7 = Resistor [tolerance=±5% resistance=0 package="1206 [SMD]"]
  J8 = Resistor [tolerance=±5% resistance=0 package="1206 [SMD]"]
  J9 = Resistor [tolerance=±5% resistance=0 package="1206 [SMD]"]
  J10 = Resistor [tolerance=±5% resistance=0 package="1206 [SMD]"]

nets:
  N1: U1.G$1_OUT1, C5.1, R6.Pin_1, J1.Pin_0
  mute: U1.G$1_-IN1, Q5.1, R2.Pin_1, C5.0, R6.Pin_0
  N2: U1.G$1_+IN1, J2.Pin_1
  GND: U1.G$1_GND, Q1.2, Q2.2, U2.Pin_1, C4.1, R4.Pin_1, R5.Pin_1, C7.1, R8.Pin_1, R9.Pin_1, C10.1, C12.1, C1.-, R18.Pin_1, C2.-, R14.Pin_1, C13.0, C11.0, JP2.1, JP1.1, Q4.2, J6.Pin_0, J6.Pin_1, J7.Pin_0, J7.Pin_1, J8.Pin_0, J8.Pin_1, J9.Pin_0, J9.Pin_1, J10.Pin_0, J10.Pin_1
  N3: U1.G$2_+IN2, R5.Pin_0, R7.Pin_0, C6.0
  N4: U1.G$2_-IN2, J3.Pin_0
  N5: U1.G$2_OUT2, R7.Pin_1, R10.Pin_0, C6.1
  5V: U1.G$1_+V, U2.Pin_8, R1.Pin_1, C7.0, R11.Pin_0, R12.Pin_0, C1.+, C2.+, JP1.2, JP3.1, J4.Pin_0, J5.Pin_0
  N6: Q5.2, R14.Pin_0
  N7: Q5.0, R15.Pin_0
  N8: Q1.0, R10.Pin_1
  N9: Q1.1, U2.Pin_2, R11.Pin_1
  N10: Q2.0, R13.Pin_1, R15.Pin_1, C13.1
  N11: Q2.1, R16.Pin_1
  N12: Q3.2, R17.Pin_1
  N13: Q3.0, R16.Pin_0
  N14: Q3.1, R18.Pin_0, Q4.0
  N15: U2.Pin_3, R13.Pin_0
  N16: U2.Pin_5, C12.0
  N17: U2.Pin_6, U2.Pin_7, R12.Pin_1, C11.1
  N18: R1.Pin_0, C3.0, JP2.2
  N19: C3.1, R2.Pin_0
  N20: C4.0, R4.Pin_0, R3.Pin_1, J2.Pin_0
  N21: C9.0, J1.Pin_1
  N22: C9.1, R8.Pin_0, D1.A
  N23: R9.Pin_0, C10.0, D1.C, J3.Pin_1
  N24: R17.Pin_0, J5.Pin_1
  N25: R3.Pin_0, J4.Pin_1
  N26: Q4.1, JP3.2

notes:
  DELAY => R13,C10
  TIME =>  R12,C9
  JACOB
